// Logisim project FLIP8_Simulation.circ as structural Verilog: 3 circuits, main circuit main
module main (
);

  wire button_1_out, clock_1_out, n7_segment_display_1_p1, n7_segment_display_2_p1, n7_segment_display_3_p1;
  wire [1:0] rom_1_data_3;
  wire [2:0] rom_1_data_2;
  wire [5:3] rom_1_data;
  wire [7:0] counter_1_q;

  Button button_1 (.out(button_1_out));
  Clock clock_1 (.out(clock_1_out));
  Counter counter_1 (.clr(button_1_out), .clk(clock_1_out), .Q(counter_1_q));  // open: load, up, count, D, carry
  ROM rom_1 (.addr(counter_1_q), .data({rom_1_data_3, rom_1_data, rom_1_data_2}));
  // _7_Segment_Display 7_segment_display_1: pin names not known; wires that end beside it: n7_segment_display_1_p1, n7_segment_display_1_p1
  // _7_Segment_Display 7_segment_display_2: pin names not known; wires that end beside it: n7_segment_display_2_p1, n7_segment_display_2_p1
  // BCD_to_7_Segment_decoder bcd_to_7_segment_decoder_1: pin names not known
  // BCD_to_7_Segment_decoder bcd_to_7_segment_decoder_2: pin names not known
  // Binary_to_BCD_converter #(.binvalue(8)) binary_to_bcd_converter_1: pin names not known; wires that end beside it: {rom_1_data_3, rom_1_data, rom_1_data_2}
  // _7_Segment_Display 7_segment_display_3: pin names not known; wires that end beside it: n7_segment_display_3_p1, n7_segment_display_3_p1
  // BCD_to_7_Segment_decoder bcd_to_7_segment_decoder_3: pin names not known
  Decoder #(.select(3)) decoder_1 (.sel(rom_1_data));  // open: out0, out1, out2, out3, out4, out5, out6, out7, en
  Decoder #(.select(3)) decoder_2 (.sel(rom_1_data_2));  // open: out0, out1, out2, out3, out4, out5, out6, out7, en
  Decoder #(.select(2)) decoder_3 (.sel(rom_1_data_3));  // open: out0, out1, out2, out3, en
  Register register_1 ();  // open: D, en, clk, Q, clr

  // Notes on the sheet:
  //   contents of rom_1 (hex, n*v repeats v):
  //   ff 3f ca
endmodule

module fullAdder (
  input  carryIn,
  input  num1,
  input  num2,
  output sum,
  output carryOut
);

  wire and_1_out, and_2_out, xor_1_out;

  xor xor_1 (xor_1_out, carryIn, num1);
  and and_1 (and_1_out, carryIn, num1);
  and and_2 (and_2_out, num2, xor_1_out);
  xor xor_2 (carryOut, xor_1_out, num2);
  or or_1 (sum, and_2_out, and_1_out);
endmodule

module eightBitAdder (
  input  carryIn,
  input  [7:0] input1,
  input  [7:0] input2,
  output [7:0] sum,
  output carryOut
);

  wire fulladder_1_carryout, fulladder_2_carryout, fulladder_3_carryout, fulladder_4_carryout,
       fulladder_5_carryout, fulladder_6_carryout, fulladder_7_carryout;

  fullAdder fulladder_1 (
    .carryIn(carryIn), .num1(input2[0]), .num2(input1[0]), .sum(sum[0]), .carryOut(fulladder_1_carryout));
  fullAdder fulladder_2 (
    .carryIn(fulladder_7_carryout), .num1(input2[4]), .num2(input1[4]), .sum(sum[4]),
    .carryOut(fulladder_2_carryout));
  fullAdder fulladder_3 (
    .carryIn(fulladder_1_carryout), .num1(input2[1]), .num2(input1[1]), .sum(sum[1]),
    .carryOut(fulladder_3_carryout));
  fullAdder fulladder_4 (
    .carryIn(fulladder_2_carryout), .num1(input2[5]), .num2(input1[5]), .sum(sum[5]),
    .carryOut(fulladder_4_carryout));
  fullAdder fulladder_5 (
    .carryIn(fulladder_3_carryout), .num1(input2[2]), .num2(input1[2]), .sum(sum[2]),
    .carryOut(fulladder_5_carryout));
  fullAdder fulladder_6 (
    .carryIn(fulladder_4_carryout), .num1(input2[6]), .num2(input1[6]), .sum(sum[6]),
    .carryOut(fulladder_6_carryout));
  fullAdder fulladder_7 (
    .carryIn(fulladder_5_carryout), .num1(input2[3]), .num2(input1[3]), .sum(sum[3]),
    .carryOut(fulladder_7_carryout));
  fullAdder fulladder_8 (
    .carryIn(fulladder_6_carryout), .num1(input2[7]), .num2(input1[7]), .sum(sum[7]), .carryOut(carryOut));
endmodule
