// Logisim project FLIP8_TTL.circ as structural Verilog: 2 circuits, main circuit main
module main (
);

  wire CKL, COUNT_OWR, n7_segment_display_1_p1, n7_segment_display_2_p1, n7_segment_display_3_p1,
       n7404_1_pin1, n7404_1_pin2, n7404_1_pin3, n7404_1_pin4, n7404_1_pin5, n7404_1_pin6, n7404_1_pin8,
       n7404_1_pin9, n7404_1_pin10, n7404_1_pin11, n7404_1_pin12, n7404_1_pin13, n7404_2_pin4, n7404_2_pin6,
       n7404_2_pin8, n7404_2_pin9, n7404_2_pin10, n7404_2_pin11, n7404_3_pin1, n7404_3_pin2, n7404_3_pin3,
       n7404_3_pin4, n7404_3_pin5, n7404_3_pin6, n7404_3_pin8, n7404_3_pin9, n7404_3_pin10, n7404_3_pin11,
       n7404_3_pin12, n7404_3_pin13, n74138_1_pin4, n74138_1_pin6, n74138_1_pin14, n74138_1_pin15,
       n74138_2_pin4, n74138_2_pin6, n74161_1_pin1, n74161_1_pin7, n74161_1_pin8, n74161_1_pin10,
       n74161_1_pin16, n74161_2_pin8, not_1_out, RESET;
  wire [7:0] n74161_2_pin3, n74161_2_pin14, rom_1_data;

  Button button_1 (.out(COUNT_OWR));
  Button button_2 (.out(RESET));
  Clock clock_1 (.out(CKL));
  not not_1 (not_1_out, COUNT_OWR);
  _74161 #(.ShowInternalStructure("true"), .VccGndPorts("true")) u_74161_1 (
    .pin1(n74161_1_pin1), .pin2(CKL), .pin3(n74161_2_pin3[4]), .pin4(n74161_2_pin3[5]),
    .pin5(n74161_2_pin3[6]), .pin6(n74161_2_pin3[7]), .pin7(n74161_1_pin7), .pin8(n74161_1_pin8),
    .pin16(n74161_1_pin16), .pin14(n74161_2_pin14[4]), .pin13(n74161_2_pin14[5]), .pin12(n74161_2_pin14[6]),
    .pin11(n74161_2_pin14[7]), .pin10(n74161_1_pin10), .pin9(not_1_out));  // open: pin15
  not not_2 (n74161_1_pin1, RESET);
  _74161 #(.ShowInternalStructure("true"), .VccGndPorts("true")) u_74161_2 (
    .pin1(n74161_1_pin1), .pin2(CKL), .pin3(n74161_2_pin3[0]), .pin4(n74161_2_pin3[1]),
    .pin5(n74161_2_pin3[2]), .pin6(n74161_2_pin3[3]), .pin7(n74161_1_pin7), .pin8(n74161_2_pin8),
    .pin16(n74161_1_pin7), .pin15(n74161_1_pin10), .pin14(n74161_2_pin14[0]), .pin13(n74161_2_pin14[1]),
    .pin12(n74161_2_pin14[2]), .pin11(n74161_2_pin14[3]), .pin10(n74161_1_pin7), .pin9(not_1_out));
  // _7_Segment_Display 7_segment_display_1: pin names not known; wires that end beside it: n7_segment_display_1_p1, n7_segment_display_1_p1
  // BCD_to_7_Segment_decoder bcd_to_7_segment_decoder_1: pin names not known
  // Binary_to_BCD_converter #(.binvalue(8)) binary_to_bcd_converter_1: pin names not known; wires that end beside it: n74161_2_pin14
  // _7_Segment_Display 7_segment_display_2: pin names not known; wires that end beside it: n7_segment_display_2_p1, n7_segment_display_2_p1
  // _7_Segment_Display 7_segment_display_3: pin names not known; wires that end beside it: n7_segment_display_3_p1, n7_segment_display_3_p1
  // BCD_to_7_Segment_decoder bcd_to_7_segment_decoder_2: pin names not known
  // BCD_to_7_Segment_decoder bcd_to_7_segment_decoder_3: pin names not known
  ROM rom_1 (.addr(n74161_2_pin14), .data(rom_1_data));
  LedBar ledbar_1 (
    .led0(rom_1_data[7]), .led1(rom_1_data[6]), .led2(rom_1_data[5]), .led3(rom_1_data[4]),
    .led4(rom_1_data[3]), .led5(rom_1_data[2]), .led6(rom_1_data[1]), .led7(rom_1_data[0]));
  _7404 #(.ShowInternalStructure("true")) u_7404_1 (
    .pin1(n7404_1_pin1), .pin2(n7404_1_pin2), .pin3(n7404_1_pin3), .pin4(n7404_1_pin4), .pin5(n7404_1_pin5),
    .pin6(n7404_1_pin6), .pin13(n7404_1_pin13), .pin12(n7404_1_pin12), .pin11(n7404_1_pin11),
    .pin10(n7404_1_pin10), .pin9(n7404_1_pin9), .pin8(n7404_1_pin8));
  _74138 #(.ShowInternalStructure("true"), .VccGndPorts("true")) u_74138_1 (
    .pin1(rom_1_data[0]), .pin2(rom_1_data[1]), .pin3(rom_1_data[2]), .pin4(n74138_1_pin4),
    .pin5(n74138_1_pin4), .pin6(n74138_1_pin6), .pin7(n7404_1_pin5), .pin8(n74138_1_pin4),
    .pin16(n74138_1_pin6), .pin15(n74138_1_pin15), .pin14(n74138_1_pin14), .pin13(n7404_1_pin9),
    .pin12(n7404_1_pin11), .pin11(n7404_1_pin13), .pin10(n7404_1_pin1), .pin9(n7404_1_pin3));
  _7404 #(.ShowInternalStructure("true")) u_7404_2 (
    .pin3(n74138_1_pin15), .pin4(n7404_2_pin4), .pin5(n74138_1_pin14), .pin6(n7404_2_pin6),
    .pin11(n7404_2_pin11), .pin10(n7404_2_pin10), .pin9(n7404_2_pin9), .pin8(n7404_2_pin8));  // open: pin1, pin2, pin13, pin12
  _7404 #(.ShowInternalStructure("true")) u_7404_3 (
    .pin1(n7404_3_pin1), .pin2(n7404_3_pin2), .pin3(n7404_3_pin3), .pin4(n7404_3_pin4), .pin5(n7404_3_pin5),
    .pin6(n7404_3_pin6), .pin13(n7404_3_pin13), .pin12(n7404_3_pin12), .pin11(n7404_3_pin11),
    .pin10(n7404_3_pin10), .pin9(n7404_3_pin9), .pin8(n7404_3_pin8));
  _74138 #(.ShowInternalStructure("true"), .VccGndPorts("true")) u_74138_2 (
    .pin1(rom_1_data[3]), .pin2(rom_1_data[4]), .pin3(rom_1_data[5]), .pin4(n74138_2_pin4),
    .pin5(n74138_2_pin4), .pin6(n74138_2_pin6), .pin7(n7404_2_pin9), .pin8(n74138_2_pin4),
    .pin16(n74138_2_pin6), .pin15(n7404_3_pin9), .pin14(n7404_3_pin11), .pin13(n7404_3_pin13),
    .pin12(n7404_3_pin1), .pin11(n7404_3_pin3), .pin10(n7404_3_pin5), .pin9(n7404_2_pin11));
  // also tied to GND on the sheet: {n74161_1_pin8, n74161_2_pin8, n74138_1_pin4, n74138_2_pin4}
  // also tied to VCC on the sheet: {n74161_1_pin16, n74161_1_pin7, n74138_1_pin6, n74138_2_pin6}

  // Notes on the sheet:
  //   contents of rom_1 (hex, n*v repeats v):
  //   ff
endmodule

module ALU (
  input  [2:0] Instruction,
  input  [7:0] Input1,
  input  [7:0] Input2
);

  wire n7404_1_pin1, n7404_1_pin2, n7404_1_pin3, n7404_1_pin4, n7404_1_pin5, n7404_1_pin6, n7404_1_pin8,
       n7404_1_pin9, n7404_1_pin10, n7404_1_pin11, n7404_1_pin12, n7404_1_pin13, n7404_2_pin4, n7404_2_pin6,
       n74138_1_pin4, n74138_1_pin6, n74138_1_pin14, n74138_1_pin15;
  wire [7:0] n7432_2_pin6;

  _7432 #(.ShowInternalStructure("true")) u_7432_1 (
    .pin1(Input1[3]), .pin2(Input2[3]), .pin3(n7432_2_pin6[3]), .pin4(Input1[2]), .pin5(Input2[2]),
    .pin6(n7432_2_pin6[2]), .pin13(Input1[7]), .pin12(Input2[7]), .pin11(n7432_2_pin6[7]), .pin10(Input1[6]),
    .pin9(Input2[6]), .pin8(n7432_2_pin6[6]));
  _7404 #(.ShowInternalStructure("true")) u_7404_1 (
    .pin1(n7404_1_pin1), .pin2(n7404_1_pin2), .pin3(n7404_1_pin3), .pin4(n7404_1_pin4), .pin5(n7404_1_pin5),
    .pin6(n7404_1_pin6), .pin13(n7404_1_pin13), .pin12(n7404_1_pin12), .pin11(n7404_1_pin11),
    .pin10(n7404_1_pin10), .pin9(n7404_1_pin9), .pin8(n7404_1_pin8));
  _7432 #(.ShowInternalStructure("true")) u_7432_2 (
    .pin1(Input1[1]), .pin2(Input2[1]), .pin3(n7432_2_pin6[1]), .pin4(Input1[0]), .pin5(Input2[0]),
    .pin6(n7432_2_pin6[0]), .pin13(Input1[5]), .pin12(Input2[5]), .pin11(n7432_2_pin6[5]), .pin10(Input1[4]),
    .pin9(Input2[4]), .pin8(n7432_2_pin6[4]));
  _74138 #(.ShowInternalStructure("true"), .VccGndPorts("true")) u_74138_1 (
    .pin1(Instruction[0]), .pin2(Instruction[1]), .pin3(Instruction[2]), .pin4(n74138_1_pin4),
    .pin5(n74138_1_pin4), .pin6(n74138_1_pin6), .pin7(n7404_1_pin5), .pin8(n74138_1_pin4),
    .pin16(n74138_1_pin6), .pin15(n74138_1_pin15), .pin14(n74138_1_pin14), .pin13(n7404_1_pin9),
    .pin12(n7404_1_pin11), .pin11(n7404_1_pin13), .pin10(n7404_1_pin1), .pin9(n7404_1_pin3));
  _7404 #(.ShowInternalStructure("true")) u_7404_2 (
    .pin3(n74138_1_pin15), .pin4(n7404_2_pin4), .pin5(n74138_1_pin14), .pin6(n7404_2_pin6));  // open: pin1, pin2, pin13, pin12, pin11, pin10, pin9, pin8
  // also tied to GND on the sheet: n74138_1_pin4
  // also tied to VCC on the sheet: n74138_1_pin6
endmodule
